// Logisim project 23_Bit_MIPS_Datapath.circ as structural Verilog: 5 circuits, main circuit 23 Bit Datapath
module _23_Bit_Datapath (
  input  in_1,
  input  in_2,
  output out_3
);

  wire and_1_out, and_2_out, clock_1_out, control_unit_1_alusrc, control_unit_1_branch, control_unit_1_cin,
       control_unit_1_jump, control_unit_1_memread, control_unit_1_memtoreg, control_unit_1_memwrite,
       control_unit_1_regdest, control_unit_1_regwrite, n23_bit_alu_1_zero, not_1_out;
  wire [1:0] control_unit_1_aluop;
  wire [4:0] bit_extender_4_out, multiplexer_1_out;
  wire [22:0] adder_1_out, adder_2_out, bit_extender_1_out, bit_extender_2_out, bit_extender_3_out,
       multiplexer_2_out, multiplexer_3_out, multiplexer_4_out, multiplexer_5_out, multiplexer_6_out,
       n23_bit_alu_1_result, n23_bit_register_file_1_read_data_1, n23_bit_register_file_1_read_data_2, PC_q,
       ram_1_data, rom_1_data;

  assign bit_extender_1_out = {{22{1'b0}}, 1'b1};  // Bit_Extender bit_extender_1
  Register #(.width(23)) PC (.D(multiplexer_5_out), .Q(PC_q), .clk(clock_1_out));  // open: en, clr
  Clock clock_1 (.out(clock_1_out));
  Adder #(.width(23)) adder_1 (.a(bit_extender_1_out), .b(PC_q), .out(adder_1_out), .cin(1'b0));  // open: cout
  Control_Unit control_unit_1 (
    .Opcode(rom_1_data[22:20]), .RegDest(control_unit_1_regdest), .Cin(control_unit_1_cin),
    .Branch(control_unit_1_branch), .Jump(control_unit_1_jump), .MemToReg(control_unit_1_memtoreg),
    .ALUsrc(control_unit_1_alusrc), .MemRead(control_unit_1_memread), .MemWrite(control_unit_1_memwrite),
    .ALUop(control_unit_1_aluop), .RegWrite(control_unit_1_regwrite));
  ROM #(.addrWidth(23), .dataWidth(23)) rom_1 (.addr(PC_q), .data(rom_1_data));  // open: sel
  assign bit_extender_2_out = {{3{1'b0}}, rom_1_data[19:0]};  // Bit_Extender bit_extender_2
  Multiplexer #(.width(5), .enable("false")) multiplexer_1 (
    .in0(rom_1_data[14:10]), .in1(rom_1_data[9:5]), .out(multiplexer_1_out), .sel(control_unit_1_regdest));
  assign bit_extender_3_out = {{13{1'b0}}, rom_1_data[9:0]};  // Bit_Extender bit_extender_3
  assign bit_extender_4_out = {{3{1'b0}}, rom_1_data[4:3]};  // Bit_Extender bit_extender_4
  _23_Bit_Register_File u_23_bit_register_file_1 (
    .Read_Data_1(n23_bit_register_file_1_read_data_1), .Write_Register_RD(multiplexer_1_out),
    .Write_Control(control_unit_1_regwrite), .Write_Data(multiplexer_6_out),
    .Read_Register_1_RS(rom_1_data[19:15]), .Read_Register_2_RT(rom_1_data[14:10]),
    .Read_Data_2(n23_bit_register_file_1_read_data_2), .Clear(in_2), .CLK(clock_1_out));
  Multiplexer #(.width(23), .enable("false")) multiplexer_2 (
    .in0(n23_bit_register_file_1_read_data_2), .in1(bit_extender_3_out), .out(multiplexer_2_out),
    .sel(control_unit_1_alusrc));
  Adder #(.width(23)) adder_2 (.a(adder_1_out), .b(bit_extender_3_out), .out(adder_2_out));  // open: cin, cout
  Multiplexer #(.width(23), .enable("false")) multiplexer_3 (
    .in0(adder_1_out), .in1(adder_2_out), .out(multiplexer_3_out), .sel(and_1_out));
  and and_1 (and_1_out, n23_bit_alu_1_zero, control_unit_1_branch);
  _23_Bit_ALU u_23_bit_alu_1 (
    .A(n23_bit_register_file_1_read_data_1), .Cin(control_unit_1_cin), .Cout(out_3),
    .Result(n23_bit_alu_1_result), .B(multiplexer_2_out), .in_5(rom_1_data[2:0]),
    .in_6(control_unit_1_aluop), .shamt(bit_extender_4_out), .zero(n23_bit_alu_1_zero));
  and and_2 (and_2_out, control_unit_1_branch, not_1_out);
  not not_1 (not_1_out, n23_bit_alu_1_zero);
  Multiplexer #(.width(23), .enable("false")) multiplexer_4 (
    .in0(multiplexer_3_out), .in1(adder_2_out), .out(multiplexer_4_out), .sel(and_2_out));
  Multiplexer #(.width(23), .enable("false")) multiplexer_5 (
    .in0(multiplexer_4_out), .in1(bit_extender_2_out), .out(multiplexer_5_out), .sel(control_unit_1_jump));
  RAM #(.addrWidth(23), .dataWidth(23), .bus("separate")) ram_1 (
    .addr(n23_bit_alu_1_result), .din(n23_bit_register_file_1_read_data_2), .data(ram_1_data),
    .str(control_unit_1_memwrite), .clk(clock_1_out), .ld(control_unit_1_memread), .clr(in_1));  // open: sel
  Multiplexer #(.width(23), .enable("false")) multiplexer_6 (
    .in0(n23_bit_alu_1_result), .in1(ram_1_data), .out(multiplexer_6_out), .sel(control_unit_1_memtoreg));

  // Notes on the sheet:
  //   function
  //   shamt
  //   rd
  //   rt
  //   rs
  //   Opcode
  //   Immediate
  //   Moontaha Rawshan (2221035642)
endmodule

module _23_Bit_ALU (
  input  [22:0] A,
  input  Cin,
  input  [22:0] B,
  input  [4:0] shamt,
  input  [2:0] in_5,
  input  [1:0] in_6,
  output zero,
  output Cout,
  output [22:0] Result
);

  wire comparator_1_lt;
  wire [2:0] alu_control_1_p1;
  wire [22:0] adder_1_out, adder_2_out, and_1_out, bit_extender_1_out, nor_1_out, not_1_out, or_1_out,
       shifter_1_out, shifter_2_out;

  assign not_1_out = ~B;  // NOT_Gate not_1, 23 bits wide
  Comparator #(.width(23)) comparator_1 (.a(A), .b(B), .eq(zero), .lt(comparator_1_lt));  // open: gt
  Shifter #(.width(23)) shifter_1 (.in(A), .\dist (shamt), .out(shifter_1_out));
  Adder #(.width(23)) adder_1 (.a(A), .b(not_1_out), .out(adder_1_out), .cin(Cin), .cout(Cout));
  assign and_1_out = A & B;  // AND_Gate and_1, 23 bits wide
  assign nor_1_out = ~(A | B);  // NOR_Gate nor_1, 23 bits wide
  assign or_1_out = A | B;  // OR_Gate or_1, 23 bits wide
  Adder #(.width(23)) adder_2 (.a(A), .b(B), .out(adder_2_out), .cin(Cin));  // open: cout
  Shifter #(.width(23), .shift("lr")) shifter_2 (.in(A), .\dist (shamt), .out(shifter_2_out));
  assign bit_extender_1_out = {{22{1'b0}}, comparator_1_lt};  // Bit_Extender bit_extender_1
  ALU_Control alu_control_1 (
    .Function(in_5), .P1(alu_control_1_p1[0]), .P2(alu_control_1_p1[1]), .P3(alu_control_1_p1[2]),
    .ALUop(in_6));  // open: out_3
  Multiplexer #(.select(3), .width(23), .enable("false")) multiplexer_1 (
    .in0(bit_extender_1_out), .in1(shifter_1_out), .in2(adder_1_out), .in3(and_1_out), .in4(nor_1_out),
    .in5(or_1_out), .in6(adder_2_out), .in7(shifter_2_out), .out(Result), .sel(alu_control_1_p1));

  // Notes on the sheet:
  //   23 Bit ALU
  //   Moontaha Rawshan (2221035642)
endmodule

module _23_Bit_Register_File (
  input  [4:0] Read_Register_1_RS,
  input  [4:0] Write_Register_RD,
  input  [4:0] Read_Register_2_RT,
  input  [22:0] Write_Data,
  input  CLK,
  input  Write_Control,
  input  Clear,
  output [22:0] Read_Data_1,
  output [22:0] Read_Data_2
);

  wire and_1_out, and_2_out, and_3_out, and_4_out, and_5_out, and_6_out, and_7_out, and_8_out, and_9_out,
       and_10_out, and_11_out, and_12_out, and_13_out, and_14_out, and_15_out, and_16_out, and_17_out,
       and_18_out, and_19_out, and_20_out, and_21_out, and_22_out, and_23_out, decoder_1_out0,
       decoder_1_out1, decoder_1_out2, decoder_1_out3, decoder_1_out4, decoder_1_out5, decoder_1_out6,
       decoder_1_out7, decoder_1_out8, decoder_1_out9, decoder_1_out10, decoder_1_out11, decoder_1_out12,
       decoder_1_out13, decoder_1_out14, decoder_1_out15, decoder_1_out16, decoder_1_out17, decoder_1_out18,
       decoder_1_out19, decoder_1_out20, decoder_1_out21, decoder_1_out22;
  wire [22:0] r0_q, r1_q, r2_q, r3_q, r4_q, r5_q, r6_q, r7_q, r8_q, r9_q, r10_q, r11_q, r12_q, r13_q, r14_q,
       r15_q, r16_q, r17_q, r18_q, r19_q, r20_q, r21_q, r22_q;

  Decoder #(.select(5), .enable("false")) decoder_1 (
    .out0(decoder_1_out0), .out1(decoder_1_out1), .out2(decoder_1_out2), .out3(decoder_1_out3),
    .out4(decoder_1_out4), .out5(decoder_1_out5), .out6(decoder_1_out6), .out7(decoder_1_out7),
    .out8(decoder_1_out8), .out9(decoder_1_out9), .out10(decoder_1_out10), .out11(decoder_1_out11),
    .out12(decoder_1_out12), .out13(decoder_1_out13), .out14(decoder_1_out14), .out15(decoder_1_out15),
    .out16(decoder_1_out16), .out17(decoder_1_out17), .out18(decoder_1_out18), .out19(decoder_1_out19),
    .out20(decoder_1_out20), .out21(decoder_1_out21), .out22(decoder_1_out22), .sel(Write_Register_RD));  // open: out23, out24, out25, out26, out27, out28, out29, out30, out31
  and and_1 (and_1_out, decoder_1_out0, Write_Control);
  and and_2 (and_2_out, decoder_1_out1, Write_Control);
  and and_3 (and_3_out, decoder_1_out2, Write_Control);
  and and_4 (and_4_out, decoder_1_out3, Write_Control);
  and and_5 (and_5_out, decoder_1_out4, Write_Control);
  and and_6 (and_6_out, decoder_1_out5, Write_Control);
  and and_7 (and_7_out, decoder_1_out6, Write_Control);
  and and_8 (and_8_out, decoder_1_out7, Write_Control);
  and and_9 (and_9_out, decoder_1_out8, Write_Control);
  and and_10 (and_10_out, decoder_1_out9, Write_Control);
  and and_11 (and_11_out, decoder_1_out10, Write_Control);
  Register #(.width(23)) r0 (.D(Write_Data), .en(and_1_out), .Q(r0_q), .clk(CLK), .clr(Clear));
  Register #(.width(23)) r1 (.D(Write_Data), .en(and_2_out), .Q(r1_q), .clk(CLK), .clr(Clear));
  Register #(.width(23)) r2 (.D(Write_Data), .en(and_3_out), .Q(r2_q), .clk(CLK), .clr(Clear));
  Register #(.width(23)) r3 (.D(Write_Data), .en(and_4_out), .Q(r3_q), .clk(CLK), .clr(Clear));
  Register #(.width(23)) r4 (.D(Write_Data), .en(and_5_out), .Q(r4_q), .clk(CLK), .clr(Clear));
  Register #(.width(23)) r5 (.D(Write_Data), .en(and_6_out), .Q(r5_q), .clk(CLK), .clr(Clear));
  Register #(.width(23)) r6 (.D(Write_Data), .en(and_7_out), .Q(r6_q), .clk(CLK), .clr(Clear));
  Register #(.width(23)) r7 (.D(Write_Data), .en(and_8_out), .Q(r7_q), .clk(CLK), .clr(Clear));
  Register #(.width(23)) r8 (.D(Write_Data), .en(and_9_out), .Q(r8_q), .clk(CLK), .clr(Clear));
  Register #(.width(23)) r9 (.D(Write_Data), .en(and_10_out), .Q(r9_q), .clk(CLK), .clr(Clear));
  Register #(.width(23)) r10 (.D(Write_Data), .en(and_11_out), .Q(r10_q), .clk(CLK), .clr(Clear));
  and and_12 (and_12_out, decoder_1_out11, Write_Control);
  and and_13 (and_13_out, decoder_1_out12, Write_Control);
  and and_14 (and_14_out, decoder_1_out13, Write_Control);
  and and_15 (and_15_out, decoder_1_out14, Write_Control);
  and and_16 (and_16_out, decoder_1_out15, Write_Control);
  and and_17 (and_17_out, decoder_1_out16, Write_Control);
  and and_18 (and_18_out, decoder_1_out17, Write_Control);
  and and_19 (and_19_out, decoder_1_out18, Write_Control);
  and and_20 (and_20_out, decoder_1_out19, Write_Control);
  and and_21 (and_21_out, decoder_1_out20, Write_Control);
  and and_22 (and_22_out, decoder_1_out21, Write_Control);
  and and_23 (and_23_out, decoder_1_out22, Write_Control);
  Register #(.width(23)) r11 (.D(Write_Data), .en(and_12_out), .Q(r11_q), .clk(CLK), .clr(Clear));
  Register #(.width(23)) r12 (.D(Write_Data), .en(and_13_out), .Q(r12_q), .clk(CLK), .clr(Clear));
  Register #(.width(23)) r13 (.D(Write_Data), .en(and_14_out), .Q(r13_q), .clk(CLK), .clr(Clear));
  Register #(.width(23)) r14 (.D(Write_Data), .en(and_15_out), .Q(r14_q), .clk(CLK), .clr(Clear));
  Register #(.width(23)) r15 (.D(Write_Data), .en(and_16_out), .Q(r15_q), .clk(CLK), .clr(Clear));
  Register #(.width(23)) r16 (.D(Write_Data), .en(and_17_out), .Q(r16_q), .clk(CLK), .clr(Clear));
  Register #(.width(23)) r17 (.D(Write_Data), .en(and_18_out), .Q(r17_q), .clk(CLK), .clr(Clear));
  Register #(.width(23)) r18 (.D(Write_Data), .en(and_19_out), .Q(r18_q), .clk(CLK), .clr(Clear));
  Register #(.width(23)) r19 (.D(Write_Data), .en(and_20_out), .Q(r19_q), .clk(CLK), .clr(Clear));
  Register #(.width(23)) r20 (.D(Write_Data), .en(and_21_out), .Q(r20_q), .clk(CLK), .clr(Clear));
  Register #(.width(23)) r21 (.D(Write_Data), .en(and_22_out), .Q(r21_q), .clk(CLK), .clr(Clear));
  Register #(.width(23)) r22 (.D(Write_Data), .en(and_23_out), .Q(r22_q), .clk(CLK), .clr(Clear));
  Multiplexer #(.select(5), .width(23), .enable("false")) multiplexer_1 (
    .in0(r0_q), .in1(r1_q), .in2(r2_q), .in3(r3_q), .in4(r4_q), .in5(r5_q), .in6(r6_q), .in7(r7_q),
    .in8(r8_q), .in9(r9_q), .in10(r10_q), .in11(r11_q), .in12(r12_q), .in13(r13_q), .in14(r14_q),
    .in15(r15_q), .in16(r16_q), .in17(r17_q), .in18(r18_q), .in19(r19_q), .in20(r20_q), .in21(r21_q),
    .in22(r22_q), .out(Read_Data_1), .sel(Read_Register_1_RS));  // open: in23, in24, in25, in26, in27, in28, in29, in30, in31
  Multiplexer #(.select(5), .width(23), .enable("false")) multiplexer_2 (
    .in0(r0_q), .in1(r1_q), .in2(r2_q), .in3(r3_q), .in4(r4_q), .in5(r5_q), .in6(r6_q), .in7(r7_q),
    .in8(r8_q), .in9(r9_q), .in10(r10_q), .in11(r11_q), .in12(r12_q), .in13(r13_q), .in14(r14_q),
    .in15(r15_q), .in16(r16_q), .in17(r17_q), .in18(r18_q), .in19(r19_q), .in20(r20_q), .in21(r21_q),
    .in22(r22_q), .out(Read_Data_2), .sel(Read_Register_2_RT));  // open: in23, in24, in25, in26, in27, in28, in29, in30, in31

  // Notes on the sheet:
  //   Design of a 23 Bit Register File
  //   Moontaha Rawshan (2221035642)
endmodule

module Control_Unit (
  input  [2:0] Opcode,
  output RegDest,
  output Cin,
  output Branch,
  output Jump,
  output MemToReg,
  output ALUsrc,
  output MemRead,
  output MemWrite,
  output [1:0] ALUop,
  output RegWrite
);

  wire decoder_1_out3, decoder_1_out4, decoder_1_out5, decoder_1_out6;

  Decoder #(.select(3), .enable("false")) decoder_1 (
    .out0(RegDest), .out1(Jump), .out2(MemToReg), .out3(decoder_1_out3), .out4(decoder_1_out4),
    .out5(decoder_1_out5), .out6(decoder_1_out6), .out7(MemWrite), .sel(Opcode));
  or or_1 (Cin, RegDest, decoder_1_out5, decoder_1_out6);
  or or_2 (Branch, decoder_1_out5, decoder_1_out6);
  or or_3 (ALUsrc, MemToReg, decoder_1_out3, MemWrite);
  or or_4 (MemRead, MemToReg, decoder_1_out3);
  or or_5 (ALUop[0], MemToReg, decoder_1_out3, MemWrite);
  or or_6 (ALUop[1], RegDest, decoder_1_out5, decoder_1_out6);
  or or_7 (RegWrite, RegDest, MemToReg, decoder_1_out3);

  // Notes on the sheet:
  //   Control Unit
  //   Moontaha Rawshan (2221035642)
endmodule

module ALU_Control (
  input  [1:0] ALUop,
  input  [2:0] Function,
  output out_3,
  output P1,
  output P2,
  output P3
);

  wire ADD_out, AND_out, decoder_1_out0, decoder_1_out1, decoder_1_out2, decoder_1_out3, decoder_1_out4,
       decoder_1_out5, decoder_1_out6, decoder_1_out7, decoder_2_out0, decoder_2_out1, decoder_2_out2,
       decoder_2_out3, NOR_out, or_2_out, or_3_out, OR_out, SLL_out, SRL_out, SUB_out;

  Decoder #(.select(3), .enable("false")) decoder_1 (
    .out0(decoder_1_out0), .out1(decoder_1_out1), .out2(decoder_1_out2), .out3(decoder_1_out3),
    .out4(decoder_1_out4), .out5(decoder_1_out5), .out6(decoder_1_out6), .out7(decoder_1_out7), .sel(Function));
  Decoder #(.select(2), .enable("false")) decoder_2 (
    .out0(decoder_2_out0), .out1(decoder_2_out1), .out2(decoder_2_out2), .out3(decoder_2_out3), .sel(ALUop));
  and SLT (out_3, decoder_2_out2, decoder_1_out0);
  and SLL (SLL_out, decoder_1_out1, decoder_2_out2);
  and SUB (SUB_out, decoder_1_out2, decoder_2_out2);
  and AND (AND_out, decoder_1_out3, decoder_2_out2);
  and NOR (NOR_out, decoder_1_out4, decoder_2_out2);
  and OR (OR_out, decoder_2_out2, decoder_1_out5);
  and ADD (ADD_out, decoder_1_out6, decoder_2_out2);
  and SRL (SRL_out, decoder_1_out7, decoder_2_out2);
  or or_2 (or_2_out, SUB_out, decoder_2_out0);
  or or_3 (or_3_out, ADD_out, decoder_2_out1);
  or or_4 (P1, SLL_out, AND_out, OR_out, SRL_out);
  or or_5 (P2, or_2_out, AND_out, or_3_out, SRL_out);
  or or_6 (P3, NOR_out, OR_out, or_3_out, SRL_out);

  // Notes on the sheet:
  //   ALU Control
  //   Moontaha Rawshan (2221035642)
endmodule
